# Fritzing sketch arduipometeo_1.5 (saved by Fritzing 0.9.3b)
circuit board: 9cm x 7cm
breadboards: 1

parts:
  R1 = Resistor [tolerance=±5% resistance=6.8k package=THT]
  R2 = Resistor [tolerance=±5% resistance=5.6k package=THT]
  BMP280 = GY-BMEP280 Barometric Pressure Sensor - Breakout
  DHT22 = DHT22 Humidity and Temperature Sensor
  C1 = Ceramic Capacitor [capacitance=0.1µF package="200 mil [THT, multilayer]"]
  Anemometro_Reed_Switch = Reed switch [package=THT]
  LED1 = LED - 5mm [color="Red (633nm)" package="5 mm [THT]"]
  ARDUINO_UNO = Arduino Uno (Rev3)-TopMount
  R3 = Resistor [tolerance=±5% resistance=220 package=THT]
  DS3231_RTC1 = ZS-042 RTC Module
  SD_Card = my_sdCard

nets:
  N1: R1.Pin_0, C1.0, Anemometro_Reed_Switch.pin_1, ARDUINO_UNO.D3_PWM
  N2: R1.Pin_1, R2.Pin_0
  VDD: R2.Pin_1, DHT22.VDD, ARDUINO_UNO.5V, SD_Card.VCC
  VCC: BMP280.VCC, BMP280.SDO, ARDUINO_UNO.3V3, DS3231_RTC1.VCC
  GND: BMP280.GND, DHT22.GND, C1.1, Anemometro_Reed_Switch.pin_2, LED1.cathode, ARDUINO_UNO.GND, DS3231_RTC1.GND, SD_Card.GND
  N3: BMP280.SCL, ARDUINO_UNO.A5/SCL, DS3231_RTC1.SCL
  N4: BMP280.SDA, ARDUINO_UNO.A4/SDA, DS3231_RTC1.SDA
  N5: DHT22.DATA, ARDUINO_UNO.D7
  N6: LED1.anode, R3.Pin_1
  N7: ARDUINO_UNO.D9_PWM, R3.Pin_0
  N8: ARDUINO_UNO.D11_PWM/MOSI, SD_Card.MOSI
  N9: ARDUINO_UNO.D12/MISO, SD_Card.MISO
  N10: ARDUINO_UNO.D13/SCK, SD_Card.SCK
  N11: ARDUINO_UNO.D4, SD_Card.CS

notes:
  IZ0QWM - http://www.kwos.it
  arduipometeo 1.5
  Anemometro Vortex Inspeed
  SD CARD
  BMP280
  DHT22
  DS3231
  +
  -
  GND
  VCC
  MISO
  MOSI
  SCK
  CS
  SDO
  SDA
  SCL
  OUT

custom parts:
  GY-BMEP280 Barometric Pressure Sensor - Breakout: The BME280 is a chip which was originally designed for the next generation of smartphones. It is made up of a very accurate pressure sensor and an associated temperature sensor which helps calibrate the pressure readings. And just for fun they threw in a pretty solid humidity sensor in there as well! So with an I2C connection you have access to enough weather data to make some pretty good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
  Arduino Uno (Rev3)-TopMount: Arduino Uno (Rev3) for Top PCB Mount. The PCB view of the Arduino Uno (Rev3) in Arduino Bin flipped upside down with the text flipped back so as to be readable. Other views haven't changed Protruding component position is outlined to provide indication of part contact. Number in component outline is mm of protrusion of the component from the UNO PCB. Subtract the number from the USB (11mm),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
  my_sdCard: micro sdCard Adapter with 90º pin header. Use a filtering Capacitor between CS and GND if needed. PCB View Pinouts are Reversed for laying parallel on PCB using a 90º pin header.

// code stored in the sketch: arduipometeo.ino
/* Stazione meteo ipogea
   Raffaello Di Martino IZ0QWM
   http://www.kwos.it */

//Libraries
#include <DHT.h>
#include "RTClib.h"
#include <DS3231.h> // http://www.rinkydinkelectronics.com/library.php?id=73
#include <SPI.h>
#include <SD.h>
#include <Wire.h>
#include <stdio.h>
#include <Adafruit_Sensor.h>
#include <Adafruit_BMP280.h>

//Costanti generiche
int i = 0;
#define PIN_LED 9

//Costanti per termometro
#define DHTPIN 7     // PIN a cui e' collegato il DHT22
#define DHTTYPE DHT22   // DHT 22  (AM2302)
DHT dht(DHTPIN, DHTTYPE); //// Initialize DHT sensor for normal 16mhz Arduino

//Costanti per anemometro
#define PIN_ANEMOMETER 3 // Digital 3
// Tempo di aggiornamento della velocita' del vento
#define MSECS_CALC_WIND_SPEED 5000

//Variabili per anemometro
volatile int numRevsAnemometer = 0; // Incrementato nella funzione countAnemometer()

File logfile;

//Start Modulo RTC 
DS3231  rtca(SDA, SCL); //Solo per leggere
RTC_DS3231 rtc; //RTC DS3231 object per settare l'orario

//Start modulo BMP280
Adafruit_BMP280 bme; // su I2C

void setup()
{
  
  Serial.begin(9600);
  //Led
  pinMode(PIN_LED, OUTPUT);
  //Anemometro
  pinMode(PIN_ANEMOMETER, INPUT);
  digitalWrite(PIN_ANEMOMETER, HIGH);
  attachInterrupt(1, countAnemometer, FALLING);
  // Realtime Clock
  rtca.begin(); // Solo per leggere
  rtc.begin(); // Solo per settare l'orario
  // Sensore pressione
  bme.begin();
  //Serial.print("---------------------------------------------------\n");
  //Serial.print("INIZIALIZZAZIONE\n");
  //Serial.print("---------------------------------------------------\n");
  //Serial.print("Setto l'orario per il log file...\n");
  rtc.adjust(DateTime(F(__DATE__), F(__TIME__))); //Prendiamo l'orario dal PC

  //SD Card
  //Serial.print("Inizializzazione SD Card...\n");

  if (!SD.begin(4)) {// Usiamo il pin 4 dove c'e' il CS per capire se la scheda e' inserita
    //Serial.println("Inizializzazione fallita!\n");
    while (1);
  }
  //Serial.println("Inizializzazione OK.\n");  
  
}

void loop()
{
    digitalWrite(PIN_LED, HIGH); 
    // create a new file
    char filename[] = "LOGGER00.CSV";
    for (uint8_t i = 0; i < 100; i++) {
      filename[6] = i/10 + '0';
      filename[7] = i%10 + '0';
      if (! SD.exists(filename)) {
        //logfile.close();
        logfile = SD.open(filename, FILE_WRITE); 
        // Serial.println("GIORNO,ORA,HUM,TEMPOUT,TEMPINT,WIND,TEMPBARO,PRESS");
        logfile.println("GIORNO,ORA,HUM,TEMPOUT,TEMPINT,WIND,TEMPBARO,PRESS\n");
        logfile.close();
        delay(1000);
      }
      logfile = SD.open(filename, FILE_WRITE);
      delay(500); 
      //Serial.println(logfile.size());
      if (logfile.size() < 200000) {  // dimensione massima del file di log in bytes
        logfile.close();        
        break;  // esco dal loop!   
      }
      logfile.close();  // Chiudo sempre. ARDUINO non gestisce più di un file aperto
    } 
    logfile = SD.open(filename, FILE_WRITE);
    delay(500);
    String TempHum = calcTempHumidity();
    //Prendo la stringa dalla funzione WindSpeed
    String Wind = calcWindSpeed();
    //Prendo la stringa dalla funzione calcPressure
    String Pressure = calcPressure();
    //Creo la stringa completa
    //String total = DataOra + "," + TempHum + "," + Wind + "," + Pressure;
    logfile.print(rtca.getDateStr());
    logfile.print(",");
    logfile.print(rtca.getTimeStr());
    //logfile.print(DataOra);
    logfile.print(",");
    logfile.print(TempHum);
    logfile.print(",");
    logfile.print(Wind);
    logfile.print(",");
    logfile.print(Pressure);
    logfile.println();
    logfile.close();

    Serial.print(rtca.getDateStr());
    Serial.print(",");
    Serial.print(rtca.getTimeStr());
    Serial.print(",");
    Serial.print(TempHum);
    Serial.print(",");
    Serial.print(Wind);
    Serial.print(",");
    Serial.print(Pressure);
    Serial.print(" -> ");
    Serial.print(filename);
    Serial.println();
    
    digitalWrite(PIN_LED, LOW);
    
    // Azzero le rivoluzioni dell'anemometro
    numRevsAnemometer = 0;
    
    delay(5000); //Delay 5 sec.

}

//=======================================================
// Interrupt handler for anemometer. Richiamato ogni volta che il reedswitch
// si attiva (un giro - revolution).
//=======================================================
void countAnemometer() {
numRevsAnemometer++;
}

String calcTempHumidity() {
    //Variabili per termometro
    float hum;  //Valore umidita' DHT
    float tempOut; //Valore temperatura DHT
    float tempIn;//Valore temperatura DS3231
    dht.begin();
    tempIn = rtca.getTemp();
    //Leggi i dati di temperatura e umidita' e inserisci nelle variabili
    hum = dht.readHumidity();
    tempOut = dht.readTemperature();
    String separatore = ",";
    String hum_temp = hum + separatore + tempOut + separatore + tempIn;
    //Serial.println(hum_temp);
    return hum_temp;
  
}


String calcPressure() {
    float tempBmp;
    tempBmp = bme.readTemperature();
    //Serial.print(bme.readTemperature());
    float pascal, hpa;
    pascal = bme.readPressure();
    //Serial.print(bme.readPressure());
    hpa = pascal * 0.01;
    
    String separatore = ",";
    //Serial.print(meters);
    String temp_press = tempBmp + separatore + hpa;
    //Serial.print(pascal);
    return temp_press;   
} 

//=======================================================
// Calcola la velocita' del vento.
// 1 rev/sec = 2.5 mph
//=======================================================
String calcWindSpeed() {
int y, x, iSpeed;
// This will produce mph * 10
// (didn't calc right when done as one statement)
long speed = 25000;//2.5 mph * 1000
speed *= numRevsAnemometer;
speed /= MSECS_CALC_WIND_SPEED;
iSpeed = speed; // Need this for formatting below

x = iSpeed / 10; // Valore in mph
y = x * 1.60934; // Trasformo in Km/h
String punto = ".";
//Serial.print('.');
x = iSpeed % 10;
String wind = y + punto + x;
return wind;
//Serial.println(wind);
numRevsAnemometer = 0; // Resetta il contatore
}
